// Logisim project main.circ as structural Verilog: 4 circuits, main circuit main
module main (
  input  [31:0] Input_1,
  input  [2:0] ALU_OP,
  input  [31:0] Input_2,
  input  [31:0] Write_Data,
  input  RegWrite,
  input  [1:0] Write_Register,
  input  [1:0] REadRegsister1,
  input  [1:0] ReadRegister2,
  output [31:0] Result,
  output out_10,
  output [31:0] ReadData1,
  output [31:0] readData2
);

  wire clock_1_out;

  Add_pc add_pc_1 ();  // open: input1, input2, Output
  Add_pc add_pc_2 ();  // open: input1, input2, Output
  ALU Alu (.Operand_1(Input_1), .Operand_2(Input_2), .Zero_Flag(out_10), .ALU_Op(ALU_OP), .Output(Result));
  Clock clock_1 (.out(clock_1_out));
  // RegisterFile registerfile_1: pin names not known; wires that end beside it: Write_Data, RegWrite, Write_Register, REadRegsister1, ReadRegister2, ReadData1, clock_1_out, readData2

  // Other names for the same wires on the sheet: in1[31:0] = Input_1; in2[31:0] = Input_2
endmodule

module ALU (
  input  [31:0] Operand_1,
  input  [31:0] Operand_2,
  input  [2:0] ALU_Op,
  output [31:0] Output,
  output Zero_Flag
);

  wire comparator_1_lt;
  wire [31:0] adder_1_out, And_out, bit_extender_1_out, Or_out, subtractor_1_out;

  Adder #(.width(32)) adder_1 (.a(Operand_1), .b(Operand_2), .out(adder_1_out));  // open: cin, cout
  Subtractor #(.width(32)) subtractor_1 (.a(Operand_1), .b(Operand_2), .out(subtractor_1_out));  // open: bin, bout
  assign And_out = Operand_1 & Operand_2;  // AND_Gate And, 32 bits wide
  assign Or_out = Operand_1 | Operand_2;  // OR_Gate Or, 32 bits wide
  Comparator #(.width(32)) comparator_1 (
    .a(Operand_1), .b(Operand_2), .eq(Zero_Flag), .lt(comparator_1_lt));  // open: gt
  assign bit_extender_1_out = {{31{1'b0}}, comparator_1_lt};  // Bit_Extender bit_extender_1
  Multiplexer #(.select(3), .width(32), .enable("false")) multiplexer_1 (
    .in0(adder_1_out), .in1(subtractor_1_out), .in2(And_out), .in3(Or_out), .in4(bit_extender_1_out),
    .out(Output), .sel(ALU_Op));  // open: in5, in6, in7
endmodule

module Add_pc (
  input  [31:0] input1,
  input  [31:0] input2,
  output [31:0] Output
);

  Adder #(.width(32)) adder_1 (.a(input1), .b(input2), .out(Output));  // open: cin, cout
endmodule

module RegisterFile (
  input  [31:0] Write_Data,
  input  [1:0] Read_register_1,
  input  Clk,
  input  Register_Write,
  input  [1:0] Write_Register,
  input  [1:0] Read_Register_2,
  output [31:0] ReadData1,
  output [31:0] REadDAta2
);

  wire decoder_1_out0, decoder_1_out1, decoder_1_out2, decoder_1_out3;
  wire [31:0] Reg0, Reg1, Reg2, Reg3;

  Decoder #(.select(2)) decoder_1 (
    .out0(decoder_1_out0), .out1(decoder_1_out1), .out2(decoder_1_out2), .out3(decoder_1_out3),
    .sel(Write_Register), .en(Register_Write));
  Register #(.width(32)) Register_0 (.en(decoder_1_out0), .Q(Reg0), .clk(Clk));  // open: D, clr
  Register #(.width(32)) Register_1 (.D(Write_Data), .en(decoder_1_out1), .Q(Reg1), .clk(Clk));  // open: clr
  Register #(.width(32)) Register_2 (.D(Write_Data), .en(decoder_1_out2), .Q(Reg2), .clk(Clk));  // open: clr
  Register #(.width(32)) Register_3 (.D(Write_Data), .en(decoder_1_out3), .Q(Reg3), .clk(Clk));  // open: clr
  Multiplexer #(.select(2), .width(32)) multiplexer_1 (
    .in0(Reg0), .in1(Reg1), .in2(Reg2), .in3(Reg3), .out(ReadData1), .sel(Read_register_1));  // open: en
  Multiplexer #(.select(2), .width(32)) multiplexer_2 (
    .in0(Reg0), .in1(Reg1), .in2(Reg2), .in3(Reg3), .out(REadDAta2), .sel(Read_Register_2));  // open: en
endmodule
