// Logisim project main2.circ as structural Verilog
module main (
);

  wire alu_1_zero_flag, Alusrc, and_1_out, clock_1_out, control_1_branch, control_1_regdst,
       control_1_regwrite, memreg, MemtR, memW;
  wire [1:0] control_1_aluop;
  wire [3:0] alucontrol_1_alucode;
  wire [4:0] multiplexer_1_out, split_1_rd, split_1_rs, split_1_rt, split_1_shamt;
  wire [5:0] split_1_opcode;
  wire [15:0] split_1_immediate;
  wire [23:0] register_1_q;
  wire [31:0] adder_1_out, adder_2_out, alu_1_output, bit_extender_1_out, bit_extender_2_out,
       memory_1_readdata, multiplexer_2_out, multiplexer_3_out, multiplexer_4_out, ram_1_data,
       registerfile_1_readdata1, registerfile_1_readdata2, shifter_1_out;

  Clock clock_1 (.out(clock_1_out));
  Register #(.width(24)) register_1 (
    .D(multiplexer_3_out[23:0]), .Q(register_1_q), .clk(clock_1_out));  // open: en, clr
  RAM #(.addrWidth(24), .dataWidth(32)) ram_1 (
    .addr(register_1_q), .data(ram_1_data), .clk(clock_1_out));  // open: sel, ld, clr
  assign bit_extender_1_out = {{8{1'b0}}, register_1_q};  // Bit_Extender bit_extender_1
  split split_1 (
    .inst_addr(ram_1_data), .opcode(split_1_opcode), .rs(split_1_rs), .rt(split_1_rt), .rd(split_1_rd),
    .shamt(split_1_shamt), .immediate(split_1_immediate));  // open: funct
  Adder #(.width(32)) adder_1 (.a(bit_extender_1_out), .b(32'h1), .out(adder_1_out));  // open: cin, cout
  control control_1 (
    .opcode(split_1_opcode), .RegDst(control_1_regdst), .ALUSrc(Alusrc), .Branch(control_1_branch),
    .MemWrite(memW), .MemRead(memreg), .MemtoReg(MemtR), .RegWrite(control_1_regwrite),
    .ALUOp(control_1_aluop));
  Multiplexer #(.width(5), .enable("false")) multiplexer_1 (
    .in0(split_1_rt), .in1(split_1_rd), .out(multiplexer_1_out), .sel(control_1_regdst));
  RegisterFile registerfile_1 (
    .Write_Data(multiplexer_4_out), .Write_enable(control_1_regwrite), .Write_register(multiplexer_1_out),
    .Read_register_1(split_1_rs), .Read_register_2(split_1_rt), .ReadData1(registerfile_1_readdata1),
    .Clk(clock_1_out), .ReadData2(registerfile_1_readdata2));
  assign bit_extender_2_out = {{16{split_1_immediate[15]}}, split_1_immediate};  // Bit_Extender bit_extender_2
  Shifter #(.width(32)) shifter_1 (.in(bit_extender_2_out), .\dist (5'b00010), .out(shifter_1_out));
  ALU alu_1 (
    .Operand_1(registerfile_1_readdata1), .Operand_2(multiplexer_2_out), .shamt(split_1_shamt),
    .Zero_Flag(alu_1_zero_flag), .alucode(alucontrol_1_alucode), .Output(alu_1_output));
  Multiplexer #(.width(32), .enable("false")) multiplexer_2 (
    .in0(registerfile_1_readdata2), .in1(bit_extender_2_out), .out(multiplexer_2_out), .sel(Alusrc));
  AluControl alucontrol_1 (.ALUOp(control_1_aluop), .funct(split_1_immediate[5:0]), .alucode(alucontrol_1_alucode));
  Adder #(.width(32)) adder_2 (.a(adder_1_out), .b(shifter_1_out), .out(adder_2_out));  // open: cin, cout
  Multiplexer #(.width(32), .enable("false")) multiplexer_3 (
    .in0(adder_1_out), .in1(adder_2_out), .out(multiplexer_3_out), .sel(and_1_out));
  and and_1 (and_1_out, control_1_branch, alu_1_zero_flag);
  memory memory_1 (
    .Address(alu_1_output[23:0]), .WriteData(registerfile_1_readdata2), .memWrite(memW), .memRead(memreg),
    .ReadData(memory_1_readdata));
  // Probe on multiplexer_3_out
  Multiplexer #(.width(32), .enable("false")) multiplexer_4 (
    .in0(memory_1_readdata), .in1(alu_1_output), .out(multiplexer_4_out), .sel(MemtR));
endmodule

module ALU (
  input  [31:0] Operand_1,
  input  [31:0] Operand_2,
  input  [3:0] alucode,
  input  [4:0] shamt,
  output [31:0] Output,
  output Zero_Flag
);

  wire comparator_1_lt;
  wire [31:0] adder_1_out, And_out, bit_extender_1_out, Or_out, shifter_1_out, subtractor_1_out;

  Adder #(.width(32)) adder_1 (.a(Operand_1), .b(Operand_2), .out(adder_1_out));  // open: cin, cout
  Subtractor #(.width(32)) subtractor_1 (.a(Operand_1), .b(Operand_2), .out(subtractor_1_out));  // open: bin, bout
  assign And_out = Operand_1 & Operand_2;  // AND_Gate And, 32 bits wide
  assign Or_out = Operand_1 | Operand_2;  // OR_Gate Or, 32 bits wide
  Comparator #(.width(32)) comparator_1 (
    .a(Operand_1), .b(Operand_2), .eq(Zero_Flag), .lt(comparator_1_lt));  // open: gt
  Shifter #(.width(32)) shifter_1 (.in(Operand_1), .\dist (shamt), .out(shifter_1_out));
  assign bit_extender_1_out = {{31{1'b0}}, comparator_1_lt};  // Bit_Extender bit_extender_1
  Multiplexer #(.select(4), .width(32), .enable("false")) multiplexer_1 (
    .in0(And_out), .in1(Or_out), .in2(adder_1_out), .in5(shifter_1_out), .in6(subtractor_1_out),
    .in7(bit_extender_1_out), .out(Output), .sel(alucode));  // open: in3, in4, in8, in9, in10, in11, in12, in13, in14, in15
endmodule

// pc
module Add_pc (
  input  [31:0] Oldpc,
  output [31:0] Next_PC
);

  Adder #(.width(32)) adder_1 (.a(Oldpc), .b(32'h1), .out(Next_PC));  // open: cin, cout
endmodule

// Register
module RegisterFile (
  input  [31:0] Write_Data,
  input  [4:0] Read_register_1,
  input  Clk,
  input  Write_enable,
  input  [4:0] Write_register,
  input  [4:0] Read_register_2,
  output [31:0] ReadData1,
  output [31:0] ReadData2
);

  wire D1, D2, D3, D4, D5, D6, D7, D8, D9, D10, D11, D12, D13, D14, D15, D17, D18, D19, D20, D21, D22, D23,
       D24, D25, D26, D27, D28, D29, D30, D31;
  wire [31:0] Reg0, Reg1, Reg2, Reg3, Reg4, Reg5, Reg6, Reg7, Reg8, Reg9, Reg10, Reg11, Reg12, Reg13, Reg14,
       Reg15, Reg16, Reg17, Reg18, Reg19, Reg20, Reg21, Reg22, Reg23, Reg24, Reg25, Reg26, Reg27, Reg28,
       Reg29, Reg30, Reg31;

  Decoder #(.select(5)) decoder_1 (
    .out1(D1), .out2(D2), .out3(D3), .out4(D4), .out5(D5), .out6(D6), .out7(D7), .out8(D8), .out9(D9),
    .out10(D10), .out11(D11), .out12(D12), .out13(D13), .out14(D14), .out15(D15), .out16(D17), .out17(D18),
    .out18(D19), .out19(D20), .out20(D21), .out21(D22), .out22(D23), .out23(D24), .out24(D25), .out25(D26),
    .out26(D27), .out27(D28), .out28(D29), .out29(D30), .out30(D31), .sel(Write_register), .en(Write_enable));  // open: out0, out31
  Register #(.width(32)) Register_0 (.Q(Reg0), .clk(Clk));  // open: D, en, clr
  Register #(.width(32)) Register_1 (.D(Write_Data), .en(D1), .Q(Reg1), .clk(Clk));  // open: clr
  Register #(.width(32)) Register_2 (.D(Write_Data), .en(D2), .Q(Reg2), .clk(Clk));  // open: clr
  Register #(.width(32)) Register_3 (.D(Write_Data), .en(D3), .Q(Reg3), .clk(Clk));  // open: clr
  Register #(.width(32)) Register_4 (.D(Write_Data), .en(D4), .Q(Reg4), .clk(Clk));  // open: clr
  Register #(.width(32)) Register_5 (.D(Write_Data), .en(D5), .Q(Reg5), .clk(Clk));  // open: clr
  Register #(.width(32)) Register_6 (.D(Write_Data), .en(D6), .Q(Reg6), .clk(Clk));  // open: clr
  Register #(.width(32)) Register_7 (.D(Write_Data), .en(D7), .Q(Reg7), .clk(Clk));  // open: clr
  Register #(.width(32)) Register_8 (.D(Write_Data), .en(D8), .Q(Reg8), .clk(Clk));  // open: clr
  Register #(.width(32)) Register_9 (.D(Write_Data), .en(D9), .Q(Reg9), .clk(Clk));  // open: clr
  Register #(.width(32)) Register_10 (.D(Write_Data), .en(D10), .Q(Reg10), .clk(Clk));  // open: clr
  Register #(.width(32)) Register_11 (.D(Write_Data), .en(D11), .Q(Reg11), .clk(Clk));  // open: clr
  Register #(.width(32)) Register_12 (.D(Write_Data), .en(D12), .Q(Reg12), .clk(Clk));  // open: clr
  Register #(.width(32)) Register_13 (.D(Write_Data), .en(D13), .Q(Reg13), .clk(Clk));  // open: clr
  Register #(.width(32)) Register_14 (.D(Write_Data), .en(D14), .Q(Reg14), .clk(Clk));  // open: clr
  Register #(.width(32)) Register_15 (.D(Write_Data), .en(D15), .Q(Reg15), .clk(Clk));  // open: clr
  Register #(.width(32)) Register_16 (.D(Write_Data), .en(D15), .Q(Reg16), .clk(Clk));  // open: clr
  Register #(.width(32)) Register_17 (.D(Write_Data), .en(D17), .Q(Reg17), .clk(Clk));  // open: clr
  Register #(.width(32)) Register_18 (.D(Write_Data), .en(D18), .Q(Reg18), .clk(Clk));  // open: clr
  Register #(.width(32)) Register_19 (.D(Write_Data), .en(D19), .Q(Reg19), .clk(Clk));  // open: clr
  Register #(.width(32)) Register_20 (.D(Write_Data), .en(D20), .Q(Reg20), .clk(Clk));  // open: clr
  Register #(.width(32)) Register_21 (.D(Write_Data), .en(D21), .Q(Reg21), .clk(Clk));  // open: clr
  Register #(.width(32)) Register_22 (.D(Write_Data), .en(D22), .Q(Reg22), .clk(Clk));  // open: clr
  Register #(.width(32)) Register_23 (.D(Write_Data), .en(D23), .Q(Reg23), .clk(Clk));  // open: clr
  Register #(.width(32)) Register_24 (.D(Write_Data), .en(D24), .Q(Reg24), .clk(Clk));  // open: clr
  Register #(.width(32)) Register_25 (.D(Write_Data), .en(D25), .Q(Reg25), .clk(Clk));  // open: clr
  Register #(.width(32)) Register_26 (.D(Write_Data), .en(D26), .Q(Reg26), .clk(Clk));  // open: clr
  Register #(.width(32)) Register_27 (.D(Write_Data), .en(D27), .Q(Reg27), .clk(Clk));  // open: clr
  Register #(.width(32)) Register_28 (.D(Write_Data), .en(D28), .Q(Reg28), .clk(Clk));  // open: clr
  Register #(.width(32)) Register_29 (.D(Write_Data), .en(D29), .Q(Reg29), .clk(Clk));  // open: clr
  Register #(.width(32)) Register_30 (.D(Write_Data), .en(D30), .Q(Reg30), .clk(Clk));  // open: clr
  Register #(.width(32)) Register_31 (.D(Write_Data), .en(D31), .Q(Reg31), .clk(Clk));  // open: clr
  Multiplexer #(.select(5), .width(32), .enable("false")) multiplexer_1 (
    .in0(Reg0), .in1(Reg1), .in2(Reg2), .in3(Reg3), .in4(Reg4), .in5(Reg5), .in6(Reg6), .in7(Reg7),
    .in8(Reg8), .in9(Reg9), .in10(Reg10), .in11(Reg11), .in12(Reg12), .in13(Reg13), .in14(Reg14),
    .in15(Reg15), .in16(Reg16), .in17(Reg17), .in18(Reg18), .in19(Reg19), .in20(Reg20), .in21(Reg21),
    .in22(Reg22), .in23(Reg23), .in24(Reg24), .in25(Reg25), .in26(Reg26), .in27(Reg27), .in28(Reg28),
    .in29(Reg29), .in30(Reg30), .in31(Reg31), .out(ReadData1), .sel(Read_register_1));
  Multiplexer #(.select(5), .width(32), .enable("false")) multiplexer_2 (
    .in0(Reg0), .in1(Reg1), .in2(Reg2), .in3(Reg3), .in4(Reg4), .in5(Reg5), .in6(Reg6), .in7(Reg7),
    .in8(Reg8), .in9(Reg9), .in10(Reg10), .in11(Reg11), .in12(Reg12), .in13(Reg13), .in14(Reg14),
    .in15(Reg15), .in16(Reg16), .in17(Reg17), .in18(Reg18), .in19(Reg19), .in20(Reg20), .in21(Reg21),
    .in22(Reg22), .in23(Reg23), .in24(Reg24), .in25(Reg25), .in26(Reg26), .in27(Reg27), .in28(Reg28),
    .in29(Reg29), .in30(Reg30), .in31(Reg31), .out(ReadData2), .sel(Read_register_2));

  // Other names for the same wires on the sheet: D16 = D15; R1[31:0] = Write_Data; R2[31:0] = Write_Data;
  //   R3[31:0] = Write_Data; R4[31:0] = Write_Data; R5[31:0] = Write_Data; R6[31:0] = Write_Data;
  //   R7[31:0] = Write_Data; R8[31:0] = Write_Data; R9[31:0] = Write_Data; R10[31:0] = Write_Data;
  //   R11[31:0] = Write_Data; R12[31:0] = Write_Data; R13[31:0] = Write_Data; R14[31:0] = Write_Data;
  //   R15[31:0] = Write_Data; R16[31:0] = Write_Data; R17[31:0] = Write_Data; R18[31:0] = Write_Data;
  //   R19[31:0] = Write_Data; R20[31:0] = Write_Data; R21[31:0] = Write_Data; R22[31:0] = Write_Data;
  //   R23[31:0] = Write_Data; R24[31:0] = Write_Data; R25[31:0] = Write_Data; R26[31:0] = Write_Data;
  //   R27[31:0] = Write_Data; R28[31:0] = Write_Data; R29[31:0] = Write_Data; R30[31:0] = Write_Data;
  //   R31[31:0] = Write_Data
endmodule

// Instruction Sp
module split (
  input  [31:0] inst_addr,
  output [5:0] opcode,
  output [4:0] rs,
  output [4:0] rt,
  output [4:0] rd,
  output [4:0] shamt,
  output [5:0] funct,
  output [15:0] immediate
);


  assign funct = inst_addr[5:0];
  assign immediate = inst_addr[15:0];
  assign opcode = inst_addr[31:26];
  assign rd = inst_addr[15:11];
  assign rs = inst_addr[25:21];
  assign rt = inst_addr[20:16];
  assign shamt = inst_addr[10:6];
endmodule

// Control
module control (
  input  [5:0] opcode,
  output RegDst,
  output ALUSrc,
  output Branch,
  output MemWrite,
  output MemRead,
  output MemtoReg,
  output RegWrite,
  output [1:0] ALUOp
);

  wire addi, and_2_out, and_3_out, andi, or_1_out, or_3_out, slti;

  and Lw (MemRead, opcode[0], opcode[1], ~opcode[2], ~opcode[3], ~opcode[4], opcode[5]);  // AND_Gate
  and Sw (MemWrite, opcode[0], opcode[1], ~opcode[2], opcode[3], ~opcode[4], opcode[5]);  // AND_Gate
  and beq (Branch, ~opcode[0], ~opcode[1], opcode[2], ~opcode[3], ~opcode[4], ~opcode[5]);  // AND_Gate
  and and_1 (RegDst, ~opcode[1], ~opcode[1], ~opcode[2], ~opcode[3], ~opcode[4], ~opcode[4]);  // AND_Gate
  and u_Addi (addi, ~opcode[0], ~opcode[1], ~opcode[2], opcode[3], ~opcode[4], ~opcode[5]);  // AND_Gate
  and u_Slti (slti, ~opcode[0], opcode[1], ~opcode[2], opcode[3], ~opcode[4], ~opcode[5]);  // AND_Gate
  and u_Andi (andi, ~opcode[0], ~opcode[1], opcode[2], opcode[3], ~opcode[4], ~opcode[5]);  // AND_Gate
  and and_2 (and_2_out, MemWrite, MemRead, RegDst);
  or or_1 (or_1_out, and_2_out, Branch, addi, slti, andi);
  or or_2 (ALUSrc, addi, MemRead, MemWrite, slti, andi);
  and and_3 (and_3_out, Branch, MemRead, MemWrite);
  or or_3 (or_3_out, andi, slti, addi, RegDst, and_3_out);
  assign ALUOp = {{1{or_3_out}}, or_1_out};  // Bit_Extender bit_extender_1
  or or_4 (RegWrite, RegDst, addi, MemRead, slti, andi);

  assign MemtoReg = MemRead;

  // Other names for the same wires on the sheet: Beq = Branch; lw = MemRead; o0 = opcode[0]; o1 = opcode[1];
  //   o2 = opcode[2]; o3 = opcode[3]; o4 = opcode[4]; o5 = opcode[5]; R = RegDst; sw = MemWrite
endmodule

// aluc
module AluControl (
  input  [1:0] ALUOp,
  input  [5:0] funct,
  output [3:0] alucode
);

  wire add_lw_sw, And, and_1_out, and_2_out, and_3_out, and_5_out, OR, sll, slt, sub_beq;

  and and_1 (and_1_out, ~ALUOp[0], ~ALUOp[1]);  // AND_Gate
  and and_2 (and_2_out, ALUOp[0], ~ALUOp[1]);  // AND_Gate
  and and_3 (and_3_out, ALUOp[0], ~ALUOp[1], ~funct[0], funct[1], ~funct[2], ~funct[3], ~funct[4], funct[5]);  // AND_Gate
  and And_4 (sll, ~ALUOp[0], ALUOp[1], ~funct[0], ~funct[1], ~funct[2], ~funct[3], ~funct[4]);  // AND_Gate
  and and_5 (and_5_out, ~ALUOp[0], ALUOp[1], ~funct[0], ~funct[1], ~funct[2], ~funct[3], ~funct[4], funct[5]);  // AND_Gate
  or or_1 (sub_beq, and_2_out, and_3_out);
  or or_2 (add_lw_sw, and_1_out, and_5_out);
  and And_6 (And, ~ALUOp[0], ALUOp[1], ~funct[0], ~funct[1], funct[2], ~funct[3], ~funct[4], funct[5]);  // AND_Gate
  and OR_3 (slt, ~ALUOp[0], ALUOp[1], ~funct[0], funct[1], ~funct[2], funct[3], ~funct[4], funct[5]);  // AND_Gate
  and and_7 (OR, ~ALUOp[0], ALUOp[1], funct[0], ~funct[1], funct[2], ~funct[3], ~funct[4], funct[5]);  // AND_Gate
  assign alucode = add_lw_sw ? 4'b0010 : 4'bz;  // Controlled_Buffer controlled_buffer_1
  assign alucode = sub_beq ? 4'b0110 : 4'bz;  // Controlled_Buffer controlled_buffer_2
  assign alucode = And ? 4'b0000 : 4'bz;  // Controlled_Buffer controlled_buffer_3
  assign alucode = OR ? 4'b0001 : 4'bz;  // Controlled_Buffer controlled_buffer_4
  assign alucode = slt ? 4'b0111 : 4'bz;  // Controlled_Buffer controlled_buffer_5
  assign alucode = sll ? 4'b0101 : 4'bz;  // Controlled_Buffer controlled_buffer_6

  // Other names for the same wires on the sheet: f0 = funct[0]; f1 = funct[1]; f2 = funct[2]; f3 = funct[3];
  //   f4 = funct[4]; f5 = funct[5]; R[1:0] = ALUOp
endmodule

// mem
module memory (
  input  [23:0] Address,
  input  [31:0] WriteData,
  input  memWrite,
  input  memRead,
  output [31:0] ReadData
);

  RAM #(.addrWidth(24), .dataWidth(32), .bus("separate")) ram_1 (
    .addr(Address), .din(WriteData), .data(ReadData), .str(memWrite), .ld(memRead));  // open: sel, clk, clr
endmodule

module IF_ID (
  input  [23:0] inPC,
  input  clock,
  input  [31:0] ini,
  output [23:0] outPC,
  output [31:0] outI
);

  Register #(.width(24)) register_1 (.D(inPC), .Q(outPC), .clk(clock));  // open: en, clr
  Register #(.width(32)) register_2 (.D(ini), .Q(outI), .clk(clock));  // open: en, clr
endmodule

module mtest (
);

  wire alu_1_zero_flag, and_1_out, clock_1_out, ex_mem_1_branch, ex_mem_1_memread, ex_mem_1_memwrite,
       ex_mem_1_zerof, id_ex_1_alusrc, id_ex_1_regdst, mem_wb_1_memtoreg, mem_wb_1_regwrite;
  wire [1:0] ex_mem_1_outwb, id_ex_1_aluop, id_ex_1_outwb, pcontrol_1_wb;
  wire [2:0] id_ex_1_outmem, pcontrol_1_mem;
  wire [3:0] alucontrol_1_alucode, pcontrol_1_ex;
  wire [4:0] ex_mem_1_outrd, id_ex_1_outrd, id_ex_1_outrt, mem_wb_1_outrd, multiplexer_3_out, shift,
       split_1_rd, split_1_rs, split_1_rt;
  wire [5:0] split_1_funct, split_1_opcode;
  wire [15:0] split_1_immediate;
  wire [23:0] adder_1_out, ex_mem_1_outbr, id_ex_1_outpc, if_id_1_outpc, multiplexer_1_out, register_1_q;
  wire [31:0] adder_2_out, alu_1_output, bit_extender_1_out, bit_extender_2_out, bit_extender_3_out,
       ex_mem_1_outalura, ex_mem_1_outwritem, id_ex_1_outoffset, id_ex_1_outrd1, id_ex_1_outrd2,
       if_id_1_outi, mem_wb_1_outalurs, mem_wb_1_outmwr, multiplexer_2_out, multiplexer_4_out, ram_1_data,
       registerfile_1_readdata1, registerfile_1_readdata2, shifter_1_out;
  wire [31:24] adder_1_out_2, ex_mem_1_outbr_2;

  Clock clock_1 (.out(clock_1_out));
  Multiplexer #(.width(24), .enable("false")) multiplexer_1 (
    .in0(adder_1_out), .in1(ex_mem_1_outbr), .out(multiplexer_1_out), .sel(and_1_out));
  assign bit_extender_1_out = {{8{1'b0}}, register_1_q};  // Bit_Extender bit_extender_1
  Register #(.width(24)) register_1 (.D(multiplexer_1_out), .Q(register_1_q), .clk(clock_1_out));  // open: en, clr
  Adder #(.width(32)) adder_1 (
    .a(bit_extender_1_out), .b(32'h1), .out({adder_1_out_2, adder_1_out}));  // open: cin, cout
  RAM #(.addrWidth(24), .dataWidth(32)) ram_1 (
    .addr(register_1_q), .data(ram_1_data), .clk(clock_1_out));  // open: sel, ld, clr
  IF_ID if_id_1 (.inPC(adder_1_out), .clock(clock_1_out), .ini(ram_1_data), .outPC(if_id_1_outpc), .outI(if_id_1_outi));
  split split_1 (
    .inst_addr(if_id_1_outi), .opcode(split_1_opcode), .rs(split_1_rs), .rt(split_1_rt), .rd(split_1_rd),
    .shamt(shift), .funct(split_1_funct), .immediate(split_1_immediate));
  // Probe on split_1_opcode
  // Probe on multiplexer_4_out
  RegisterFile registerfile_1 (
    .Write_Data(multiplexer_4_out), .Write_enable(mem_wb_1_regwrite), .Write_register(mem_wb_1_outrd),
    .Read_register_1(split_1_rs), .Read_register_2(split_1_rt), .ReadData1(registerfile_1_readdata1),
    .Clk(clock_1_out), .ReadData2(registerfile_1_readdata2));
  pCONTROL pcontrol_1 (.opcode(split_1_opcode), .EX(pcontrol_1_ex), .WB(pcontrol_1_wb), .MEM(pcontrol_1_mem));
  // Probe on bit_extender_2_out
  assign bit_extender_2_out = {{16{split_1_immediate[15]}}, split_1_immediate};  // Bit_Extender bit_extender_2
  ID_EX id_ex_1 (
    .inPC(if_id_1_outpc), .inRT(split_1_rt), .inRD(split_1_rd), .inRD1(registerfile_1_readdata1),
    .inWB(pcontrol_1_wb), .inRD2(registerfile_1_readdata2), .inMem(pcontrol_1_mem),
    .inoffsett(bit_extender_2_out), .inEx(pcontrol_1_ex), .clock(clock_1_out), .outPC(id_ex_1_outpc),
    .outRT(id_ex_1_outrt), .outRD(id_ex_1_outrd), .outRD1(id_ex_1_outrd1), .outWB(id_ex_1_outwb),
    .outRD2(id_ex_1_outrd2), .outMem(id_ex_1_outmem), .outOffset(id_ex_1_outoffset), .ALUSrc(id_ex_1_alusrc),
    .RegDst(id_ex_1_regdst), .ALUOp(id_ex_1_aluop));
  assign bit_extender_3_out = {{8{1'b0}}, id_ex_1_outpc};  // Bit_Extender bit_extender_3
  Shifter #(.width(32)) shifter_1 (.in(id_ex_1_outoffset), .\dist (5'b00010), .out(shifter_1_out));
  Multiplexer #(.width(32), .enable("false")) multiplexer_2 (
    .in0(id_ex_1_outrd2), .in1(id_ex_1_outoffset), .out(multiplexer_2_out), .sel(id_ex_1_alusrc));
  // Probe on id_ex_1_aluop
  // Probe on split_1_funct
  Multiplexer #(.width(5), .enable("false")) multiplexer_3 (
    .in0(id_ex_1_outrt), .in1(id_ex_1_outrd), .out(multiplexer_3_out), .sel(id_ex_1_regdst));
  Adder #(.width(32)) adder_2 (.a(bit_extender_3_out), .b(shifter_1_out), .out(adder_2_out));  // open: cin, cout
  // Probe on alucontrol_1_alucode
  AluControl alucontrol_1 (.ALUOp(id_ex_1_aluop), .funct(split_1_funct), .alucode(alucontrol_1_alucode));
  // Probe on alu_1_zero_flag
  ALU alu_1 (
    .Operand_1(id_ex_1_outrd1), .Operand_2(multiplexer_2_out), .shamt(shift), .Zero_Flag(alu_1_zero_flag),
    .alucode(alucontrol_1_alucode), .Output(alu_1_output));
  EX_MEM ex_mem_1 (
    .inBr(adder_2_out), .ALURAin(alu_1_output), .inWriteM(id_ex_1_outrd2), .inRD(multiplexer_3_out),
    .inWB(id_ex_1_outwb), .inMem(id_ex_1_outmem), .inZerof(alu_1_zero_flag), .memRead(ex_mem_1_memread),
    .clock(clock_1_out), .outBR({ex_mem_1_outbr_2, ex_mem_1_outbr}), .outALURA(ex_mem_1_outalura),
    .outWriteM(ex_mem_1_outwritem), .outRD(ex_mem_1_outrd), .outWB(ex_mem_1_outwb),
    .memWrite(ex_mem_1_memwrite), .branch(ex_mem_1_branch), .zeroF(ex_mem_1_zerof));
  and and_1 (and_1_out, ex_mem_1_branch, ex_mem_1_zerof);
  memory memory_1 (
    .Address(ex_mem_1_outalura[23:0]), .WriteData(ex_mem_1_outwritem), .memWrite(ex_mem_1_memwrite),
    .memRead(ex_mem_1_memread));  // open: ReadData
  MEM_WB mem_wb_1 (
    .ALURsin(ex_mem_1_outalura), .inMWR(ex_mem_1_outwritem), .inRD(ex_mem_1_outrd), .inWB(ex_mem_1_outwb),
    .clock(clock_1_out), .outALURs(mem_wb_1_outalurs), .outMWR(mem_wb_1_outmwr), .outRD(mem_wb_1_outrd),
    .RegWrite(mem_wb_1_regwrite), .MemToReg(mem_wb_1_memtoreg));
  Multiplexer #(.width(32), .enable("false")) multiplexer_4 (
    .in0(mem_wb_1_outalurs), .in1(mem_wb_1_outmwr), .out(multiplexer_4_out), .sel(mem_wb_1_memtoreg));
endmodule

module ID_EX (
  input  [23:0] inPC,
  input  [4:0] inRT,
  input  [4:0] inRD,
  input  [31:0] inRD1,
  input  [1:0] inWB,
  input  [31:0] inRD2,
  input  [2:0] inMem,
  input  [31:0] inoffsett,
  input  [3:0] inEx,
  input  clock,
  output [23:0] outPC,
  output [4:0] outRT,
  output [4:0] outRD,
  output [31:0] outRD1,
  output [1:0] outWB,
  output [31:0] outRD2,
  output [2:0] outMem,
  output [31:0] outOffset,
  output ALUSrc,
  output RegDst,
  output [1:0] ALUOp
);

  Register #(.width(24)) register_1 (.D(inPC), .Q(outPC), .clk(clock));  // open: en, clr
  Register #(.width(32)) register_2 (.D(inRD1), .Q(outRD1), .clk(clock));  // open: en, clr
  Register #(.width(32)) register_3 (.D(inRD2), .Q(outRD2), .clk(clock));  // open: en, clr
  Register #(.width(32)) register_4 (.D(inoffsett), .Q(outOffset), .clk(clock));  // open: en, clr
  Register #(.width(4)) register_5 (.D(inEx), .Q({ALUOp, RegDst, ALUSrc}), .clk(clock));  // open: en, clr
  Register #(.width(5)) register_6 (.D(inRT), .Q(outRT), .clk(clock));  // open: en, clr
  Register #(.width(5)) register_7 (.D(inRD), .Q(outRD), .clk(clock));  // open: en, clr
  Register #(.width(2)) register_8 (.D(inWB), .Q(outWB), .clk(clock));  // open: en, clr
  Register #(.width(3)) register_9 (.D(inMem), .Q(outMem), .clk(clock));  // open: en, clr
endmodule

module EX_MEM (
  input  [31:0] inBr,
  input  [31:0] ALURAin,
  input  [31:0] inWriteM,
  input  [4:0] inRD,
  input  [1:0] inWB,
  input  [2:0] inMem,
  input  inZerof,
  input  clock,
  output [31:0] outBR,
  output [31:0] outALURA,
  output [31:0] outWriteM,
  output [4:0] outRD,
  output [1:0] outWB,
  output memRead,
  output memWrite,
  output branch,
  output zeroF
);

  wire undriven;

  Register #(.width(5)) register_1 (.D(inRD), .Q(outRD), .clk(clock));  // open: en, clr
  Register #(.width(2)) register_2 (.D(inWB), .Q(outWB), .clk(clock));  // open: en, clr
  Register #(.width(3)) register_3 (.D(inMem), .Q({branch, memWrite, memRead}), .clk(clock));  // open: en, clr
  Register #(.width(1)) register_4 (.D(inZerof), .Q(zeroF), .clk(clock));  // open: en, clr
  Register #(.width(32)) register_5 (.D(inBr), .Q(outBR), .clk(clock));  // open: en, clr
  Register #(.width(32)) register_6 (.D(ALURAin), .Q(outALURA), .clk(undriven));  // open: en, clr
  Register #(.width(32)) register_7 (.D(inWriteM), .Q(outWriteM), .clk(clock));  // open: en, clr
endmodule

module MEM_WB (
  input  [31:0] ALURsin,
  input  [31:0] inMWR,
  input  [4:0] inRD,
  input  [1:0] inWB,
  input  clock,
  output [31:0] outALURs,
  output [31:0] outMWR,
  output [4:0] outRD,
  output RegWrite,
  output MemToReg
);

  Register #(.width(5)) register_1 (.D(inRD), .Q(outRD), .clk(clock));  // open: en, clr
  Register #(.width(2)) register_2 (.D(inWB), .Q({MemToReg, RegWrite}), .clk(clock));  // open: en, clr
  Register #(.width(32)) register_3 (.D(ALURsin), .Q(outALURs), .clk(clock));  // open: en, clr
  Register #(.width(32)) register_4 (.D(inMWR), .Q(outMWR), .clk(clock));  // open: en, clr
endmodule

module pCONTROL (
  input  [5:0] opcode,
  output [3:0] EX,
  output [1:0] WB,
  output [2:0] MEM
);

  wire addi, and_2_out, and_3_out, andi, or_1_out, or_2_out, slti;

  and Lw (MEM[0], opcode[0], opcode[1], ~opcode[2], ~opcode[3], ~opcode[4], opcode[5]);  // AND_Gate
  and Sw (MEM[1], opcode[0], opcode[1], ~opcode[2], opcode[3], ~opcode[4], opcode[5]);  // AND_Gate
  and beq (MEM[2], ~opcode[0], ~opcode[1], opcode[2], ~opcode[3], ~opcode[4], ~opcode[5]);  // AND_Gate
  and and_1 (EX[1], ~opcode[1], ~opcode[1], ~opcode[2], ~opcode[3], ~opcode[4], ~opcode[4]);  // AND_Gate
  and u_Addi (addi, ~opcode[0], ~opcode[1], ~opcode[2], opcode[3], ~opcode[4], ~opcode[5]);  // AND_Gate
  and u_Slti (slti, ~opcode[0], opcode[1], ~opcode[2], opcode[3], ~opcode[4], ~opcode[5]);  // AND_Gate
  and u_Andi (andi, ~opcode[0], ~opcode[1], opcode[2], opcode[3], ~opcode[4], ~opcode[5]);  // AND_Gate
  and and_2 (and_2_out, MEM[1], MEM[0], EX[1]);
  or or_1 (or_1_out, and_2_out, MEM[2], addi, slti, andi);
  and and_3 (and_3_out, MEM[2], MEM[0], MEM[1]);
  or or_2 (or_2_out, andi, slti, addi, EX[1], and_3_out);
  assign EX[3:2] = {{1{or_2_out}}, or_1_out};  // Bit_Extender bit_extender_1
  or or_3 (EX[0], addi, MEM[0], MEM[1], slti, andi);
  or or_4 (WB[0], EX[1], addi, MEM[0], slti, andi);

  assign WB[1] = MEM[0];

  // Other names for the same wires on the sheet: R = EX[1]; aluop[1:0] = EX[3:2]; lw = MEM[0]; sw = MEM[1];
  //   Beq = MEM[2]; o0 = opcode[0]; o1 = opcode[1]; o2 = opcode[2]; o3 = opcode[3]; o4 = opcode[4]; o5 = opcode[5]
endmodule

module mr (
);

  wire alu_1_zero_flag, and_1_out, clock_1_out, ex_mem_1_branch, ex_mem_1_memread, ex_mem_1_memwrite,
       ex_mem_1_zerof, id_ex_1_alusrc, id_ex_1_regdst, mem_wb_1_memtoreg, mem_wb_1_regwrite;
  wire [1:0] ex_mem_1_outwb, id_ex_1_aluop, id_ex_1_outwb, pcontrol_1_wb;
  wire [2:0] id_ex_1_outmem, pcontrol_1_mem;
  wire [3:0] alucontrol_1_alucode, pcontrol_1_ex;
  wire [4:0] ex_mem_1_outrd, id_ex_1_outrd, id_ex_1_outrt, mem_wb_1_outrd, multiplexer_3_out, shift,
       split_1_rd, split_1_rs, split_1_rt;
  wire [5:0] split_1_funct, split_1_opcode;
  wire [15:0] split_1_immediate;
  wire [23:0] adder_1_out, ex_mem_1_outbr, id_ex_1_outpc, if_id_1_outpc, multiplexer_1_out, register_1_q;
  wire [31:0] adder_2_out, alu_1_output, bit_extender_1_out, bit_extender_2_out, bit_extender_3_out,
       ex_mem_1_outalura, ex_mem_1_outwritem, id_ex_1_outoffset, id_ex_1_outrd1, id_ex_1_outrd2,
       if_id_1_outi, mem_wb_1_outalurs, mem_wb_1_outmwr, multiplexer_2_out, multiplexer_4_out, ram_1_data,
       registerfile_1_readdata1, registerfile_1_readdata2, shifter_1_out;
  wire [31:24] adder_1_out_2, ex_mem_1_outbr_2;

  Clock clock_1 (.out(clock_1_out));
  Multiplexer #(.width(24), .enable("false")) multiplexer_1 (
    .in0(adder_1_out), .in1(ex_mem_1_outbr), .out(multiplexer_1_out), .sel(and_1_out));
  assign bit_extender_1_out = {{8{1'b0}}, register_1_q};  // Bit_Extender bit_extender_1
  Register #(.width(24)) register_1 (.D(multiplexer_1_out), .Q(register_1_q), .clk(clock_1_out));  // open: en, clr
  Adder #(.width(32)) adder_1 (
    .a(bit_extender_1_out), .b(32'h1), .out({adder_1_out_2, adder_1_out}));  // open: cin, cout
  RAM #(.addrWidth(24), .dataWidth(32)) ram_1 (
    .addr(register_1_q), .data(ram_1_data), .clk(clock_1_out));  // open: sel, ld, clr
  IF_ID if_id_1 (.inPC(adder_1_out), .clock(clock_1_out), .ini(ram_1_data), .outPC(if_id_1_outpc), .outI(if_id_1_outi));
  split split_1 (
    .inst_addr(if_id_1_outi), .opcode(split_1_opcode), .rs(split_1_rs), .rt(split_1_rt), .rd(split_1_rd),
    .shamt(shift), .funct(split_1_funct), .immediate(split_1_immediate));
  RegisterFile registerfile_1 (
    .Write_Data(multiplexer_4_out), .Write_enable(mem_wb_1_regwrite), .Write_register(mem_wb_1_outrd),
    .Read_register_1(split_1_rs), .Read_register_2(split_1_rt), .ReadData1(registerfile_1_readdata1),
    .Clk(clock_1_out), .ReadData2(registerfile_1_readdata2));
  pCONTROL pcontrol_1 (.opcode(split_1_opcode), .EX(pcontrol_1_ex), .WB(pcontrol_1_wb), .MEM(pcontrol_1_mem));
  assign bit_extender_2_out = {{16{split_1_immediate[15]}}, split_1_immediate};  // Bit_Extender bit_extender_2
  ID_EX id_ex_1 (
    .inPC(if_id_1_outpc), .inRT(split_1_rt), .inRD(split_1_rd), .inRD1(registerfile_1_readdata1),
    .inWB(pcontrol_1_wb), .inRD2(registerfile_1_readdata2), .inMem(pcontrol_1_mem),
    .inoffsett(bit_extender_2_out), .inEx(pcontrol_1_ex), .clock(clock_1_out), .outPC(id_ex_1_outpc),
    .outRT(id_ex_1_outrt), .outRD(id_ex_1_outrd), .outRD1(id_ex_1_outrd1), .outWB(id_ex_1_outwb),
    .outRD2(id_ex_1_outrd2), .outMem(id_ex_1_outmem), .outOffset(id_ex_1_outoffset), .ALUSrc(id_ex_1_alusrc),
    .RegDst(id_ex_1_regdst), .ALUOp(id_ex_1_aluop));
  assign bit_extender_3_out = {{8{1'b0}}, id_ex_1_outpc};  // Bit_Extender bit_extender_3
  Shifter #(.width(32)) shifter_1 (.in(id_ex_1_outoffset), .\dist (5'b00010), .out(shifter_1_out));
  Multiplexer #(.width(32), .enable("false")) multiplexer_2 (
    .in0(id_ex_1_outrd2), .in1(id_ex_1_outoffset), .out(multiplexer_2_out), .sel(id_ex_1_alusrc));
  Multiplexer #(.width(5), .enable("false")) multiplexer_3 (
    .in0(id_ex_1_outrt), .in1(id_ex_1_outrd), .out(multiplexer_3_out), .sel(id_ex_1_regdst));
  Adder #(.width(32)) adder_2 (.a(bit_extender_3_out), .b(shifter_1_out), .out(adder_2_out));  // open: cin, cout
  AluControl alucontrol_1 (.ALUOp(id_ex_1_aluop), .funct(split_1_funct), .alucode(alucontrol_1_alucode));
  ALU alu_1 (
    .Operand_1(id_ex_1_outrd1), .Operand_2(multiplexer_2_out), .shamt(shift), .Zero_Flag(alu_1_zero_flag),
    .alucode(alucontrol_1_alucode), .Output(alu_1_output));
  EX_MEM ex_mem_1 (
    .inBr(adder_2_out), .ALURAin(alu_1_output), .inWriteM(id_ex_1_outrd2), .inRD(multiplexer_3_out),
    .inWB(id_ex_1_outwb), .inMem(id_ex_1_outmem), .inZerof(alu_1_zero_flag), .memRead(ex_mem_1_memread),
    .clock(clock_1_out), .outBR({ex_mem_1_outbr_2, ex_mem_1_outbr}), .outALURA(ex_mem_1_outalura),
    .outWriteM(ex_mem_1_outwritem), .outRD(ex_mem_1_outrd), .outWB(ex_mem_1_outwb),
    .memWrite(ex_mem_1_memwrite), .branch(ex_mem_1_branch), .zeroF(ex_mem_1_zerof));
  and and_1 (and_1_out, ex_mem_1_branch, ex_mem_1_zerof);
  memory memory_1 (
    .Address(ex_mem_1_outalura[23:0]), .WriteData(ex_mem_1_outwritem), .memWrite(ex_mem_1_memwrite),
    .memRead(ex_mem_1_memread));  // open: ReadData
  MEM_WB mem_wb_1 (
    .ALURsin(ex_mem_1_outalura), .inMWR(ex_mem_1_outwritem), .inRD(ex_mem_1_outrd), .inWB(ex_mem_1_outwb),
    .clock(clock_1_out), .outALURs(mem_wb_1_outalurs), .outMWR(mem_wb_1_outmwr), .outRD(mem_wb_1_outrd),
    .RegWrite(mem_wb_1_regwrite), .MemToReg(mem_wb_1_memtoreg));
  Multiplexer #(.width(32), .enable("false")) multiplexer_4 (
    .in0(mem_wb_1_outalurs), .in1(mem_wb_1_outmwr), .out(multiplexer_4_out), .sel(mem_wb_1_memtoreg));
endmodule
